# Fritzing sketch single-channel (saved by Fritzing 1.0.3b)
circuit board: 4.34588cm x 2.38071cm
breadboards: 2

parts:
  U3 = CD74HC4067 [part_number=CD74HC4067]
  D2 = BAT54S [part_number=BAT54S package=SOT23-3]
  D1 = BAT54S [part_number=BAT54S package=SOT23-3]
  R1 = Resistor [tolerance=±1% resistance=220 power=0.25W package="0603 [SMD]"]
  U2 = TS3A44159PWR [part_number=TS3A44159PWR package=TSSOP-16]
  C1 = Ceramic Capacitor [capacitance=100nF voltage=35V package="0603 [SMD, multilayer]"]
  L1 = NFC Coil [part_number=NFC-Coil-20-6T package=PCB]

nets:
  N1: U3.C0, U2.NO1
  IO1: U3.SIG
  IO4: U3.S0
  IO5: U3.S1
  IO6: U3.S2
  IO7: U3.S3
  GND: U3.EN, U3.GND, D2.A1, D1.A1, U2.GND, U2.NC1, C1.0
  3V3: U3.VCC, U2.VCC
  N2: D2.K2, D1.K2, R1.Pin_0
  N3: D2.node, L1.outer
  N4: D1.node, L1.inner
  N5: R1.Pin_1, U2.COM1, C1.1
  IO2: U2.IN3-4, U2.IN1-2

notes:
  花石箓
  NFC极光镶嵌
  v0.1.3
  J1

custom parts:
  CD74HC4067: 16-channel analog/digital multiplexer (CD74HC4067), terminals C0-C15 / SIG / S0-S3 / EN / VCC / GND.
  BAT54S: Dual series Schottky diode, SOT-23. Two diodes: pin1->pin3->pin2.
  TS3A44159PWR: Quad SPDT / dual DPDT bidirectional analog switch, 1.65-4.3 V, TSSOP-16 (PW).
  NFC Coil: 13.56 MHz NFC sensing coil (PCB spiral, 20 mm OD, 6 turns)
